# Fritzing sketch Branchement (saved by Fritzing 0.9.3b)
breadboards: 2

parts:
  Composant1 = Adafruit Latching Mini Relay FeatherWing [part_number="Adafruit #2923"]
  Composant2 = Adafruit HUZZAH32 ESP32 Feather [part_number="Adafruit #3405"]
  S1 = Toggle Switch [package=THT]
  L1 = Solenoid
  Composant3 = Adafruit DC+Stepper FeatherWing [part_number="Adafruit #2927"]

nets:
  GND: Composant1.GND, Composant2.GND, L1.pin1, Composant3.GND
  N1: Composant1.NO, L1.pin2
  N2: Composant1.COM, Composant2.A5_IO4
  N3: S1.COM, S1.L2

custom parts:
  Adafruit Latching Mini Relay FeatherWing: A Feather board without ambition is a Feather board without FeatherWings! This is the Latching Mini Relay FeatherWing. It gives you power to control, and control over power. Put simply, you can now turn on and off lamps, fans, solenoids, and other small appliances that run on up to 250VAC or DC power using any Feather board. The are two 'flavors' of these FeatherWings, this is the Latching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
  Adafruit DC+Stepper FeatherWing: This is the DC Motor + Stepper FeatherWing which will let you use 2 x bi-polar stepper motors or 4 x brushed DC motorx (or 1 stepper and 2 DC motors). Using our Feather Stacking Headers or Feather Female Headers you can connect a FeatherWing on top or bottom of your Feather board and let the board take flight! The original Adafruit Motorshield Kit is one of our most beloved kits, which is why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
